# Fritzing sketch SketchRF_OnOff (saved by Fritzing 0.9.1b)
breadboards: 1

parts:
  U1 = RF-LINK_RX [package=rf-link_rx]
  Part1 = Arduino Pro Mini v13
  Q1 = Basic FET N-Channel [package="TO220 [THT]"]
  R1 = Resistor [tolerance=±5% resistance=220 package=THT]
  R2 = Resistor [tolerance=±5% resistance=100k package=THT]
  X1 = USB Connectors [package=usb-a-h]
  Raspberry_Pi1 = Raspberry Pi B rev2
  ANT1 = Antenna
  C1 = Ceramic Capacitor [capacitance="100 nF" package="100 mil [THT, multilayer]"]

nets:
  GND: U1.GND, Part1.GND, Q1.source, R2.Pin_1, X1.GND, C1.0
  N1: U1.DATA, Part1.D2
  +5V: U1.+5V, Part1.VCC, X1.VBUS, Raspberry_Pi1.5V, C1.1
  N2: U1.ANT, ANT1.antenna_lead
  N3: Part1.D10_PWM/SS, R1.Pin_0
  N4: Q1.gate, R1.Pin_1, R2.Pin_0
  N5: Q1.drain, Raspberry_Pi1.GND
